// Logisim project datapath.circ as structural Verilog: 1 circuit, main circuit main
module main (
  input  i_w,
  input  addr_shift,
  input  ex_shift,
  input  i_rst,
  input  s_done,
  input  data_load,
  input  [7:0] i_mem_data,
  output [15:0] o_mem_addr,
  output [7:0] o_z0,
  output [7:0] o_z1,
  output [7:0] o_z2,
  output [7:0] o_z3
);

  wire and_1_out, and_2_out, and_3_out, and_4_out, ex0_q, ex1_q, i_clk_out, or_1_out, w1_q;
  wire [7:0] z0_reg_q, z1_reg_q, z2_reg_q, z3_reg_q;

  D_Flip_Flop w1 (.D(i_w), .clk(i_clk_out), .Q(w1_q), .reset(1'b0));  // open: Qn, preset
  Register #(.width(1)) q0 (.D(w1_q), .en(addr_shift), .clk(i_clk_out), .Q(o_mem_addr[0]), .clr(or_1_out));
  Register #(.width(1)) ex0 (.D(w1_q), .en(ex_shift), .clk(i_clk_out), .Q(ex0_q), .clr(1'b0));
  Register #(.width(1)) q1 (.D(o_mem_addr[0]), .en(addr_shift), .clk(i_clk_out), .Q(o_mem_addr[1]), .clr(or_1_out));
  Register #(.width(1)) ex1 (.D(ex0_q), .en(ex_shift), .clk(i_clk_out), .Q(ex1_q), .clr(1'b0));
  Register #(.width(1)) q2 (.D(o_mem_addr[1]), .en(addr_shift), .clk(i_clk_out), .Q(o_mem_addr[2]), .clr(or_1_out));
  Register #(.width(1)) q3 (.D(o_mem_addr[2]), .en(addr_shift), .clk(i_clk_out), .Q(o_mem_addr[3]), .clr(or_1_out));
  Register #(.width(1)) q4 (.D(o_mem_addr[3]), .en(addr_shift), .clk(i_clk_out), .Q(o_mem_addr[4]), .clr(or_1_out));
  Register #(.width(1)) q5 (.D(o_mem_addr[4]), .en(addr_shift), .clk(i_clk_out), .Q(o_mem_addr[5]), .clr(or_1_out));
  Register z0_reg (.D(i_mem_data), .en(and_1_out), .clk(i_clk_out), .Q(z0_reg_q), .clr(i_rst));
  and and_1 (and_1_out, data_load, ~ex1_q, ~ex0_q);  // AND_Gate
  Register z1_reg (.D(i_mem_data), .en(and_2_out), .clk(i_clk_out), .Q(z1_reg_q), .clr(i_rst));
  and and_2 (and_2_out, data_load, ~ex1_q, ex0_q);  // AND_Gate
  Register z2_reg (.D(i_mem_data), .en(and_3_out), .clk(i_clk_out), .Q(z2_reg_q), .clr(i_rst));
  and and_3 (and_3_out, data_load, ex1_q, ~ex0_q);  // AND_Gate
  Register z3_reg (.D(i_mem_data), .en(and_4_out), .clk(i_clk_out), .Q(z3_reg_q), .clr(i_rst));
  and and_4 (and_4_out, data_load, ex1_q, ex0_q);
  Register #(.width(1)) q6 (.D(o_mem_addr[5]), .en(addr_shift), .clk(i_clk_out), .Q(o_mem_addr[6]), .clr(or_1_out));
  Register #(.width(1)) q7 (.D(o_mem_addr[6]), .en(addr_shift), .clk(i_clk_out), .Q(o_mem_addr[7]), .clr(or_1_out));
  Multiplexer #(.width(8)) multiplexer_1 (.in0({8{1'b0}}), .in1(z0_reg_q), .out(o_z0), .sel(s_done));
  Multiplexer #(.width(8)) multiplexer_2 (.in0({8{1'b0}}), .in1(z1_reg_q), .out(o_z1), .sel(s_done));
  Multiplexer #(.width(8)) multiplexer_3 (.in0({8{1'b0}}), .in1(z2_reg_q), .out(o_z2), .sel(s_done));
  Multiplexer #(.width(8)) multiplexer_4 (.in0({8{1'b0}}), .in1(z3_reg_q), .out(o_z3), .sel(s_done));
  Register #(.width(1)) q8 (.D(o_mem_addr[7]), .en(addr_shift), .clk(i_clk_out), .Q(o_mem_addr[8]), .clr(or_1_out));
  Register #(.width(1)) q9 (.D(o_mem_addr[8]), .en(addr_shift), .clk(i_clk_out), .Q(o_mem_addr[9]), .clr(or_1_out));
  Register #(.width(1)) q11 (.D(o_mem_addr[10]), .en(addr_shift), .clk(i_clk_out), .Q(o_mem_addr[11]), .clr(or_1_out));
  Register #(.width(1)) q10 (.D(o_mem_addr[9]), .en(addr_shift), .clk(i_clk_out), .Q(o_mem_addr[10]), .clr(or_1_out));
  Register #(.width(1)) q12 (.D(o_mem_addr[11]), .en(addr_shift), .clk(i_clk_out), .Q(o_mem_addr[12]), .clr(or_1_out));
  Register #(.width(1)) q13 (.D(o_mem_addr[12]), .en(addr_shift), .clk(i_clk_out), .Q(o_mem_addr[13]), .clr(or_1_out));
  Register #(.width(1)) q14 (.D(o_mem_addr[13]), .en(addr_shift), .clk(i_clk_out), .Q(o_mem_addr[14]), .clr(or_1_out));
  Register #(.width(1)) q15 (.D(o_mem_addr[14]), .en(addr_shift), .clk(i_clk_out), .Q(o_mem_addr[15]), .clr(or_1_out));
  or or_1 (or_1_out, s_done, i_rst);
  Clock i_clk (.out(i_clk_out));
endmodule
